# Fritzing sketch IFResources (saved by Fritzing 0.9.3b)
circuit board: 6.06644cm x 8.64727cm
breadboards: 1

parts:
  Heltec_WiFi_LoRa_32_V2 = Heltec WiFi LoRa 32 V2 [part_number=HTIT-WB32LA]
  Transmissor = KY-005 Infrared Transmitter Module [package="Breakout board"]
  Sensor_DHT22 = DHT22 module

nets:
  N1: Heltec_WiFi_LoRa_32_V2.pin_2, Transmissor.S
  N2: Heltec_WiFi_LoRa_32_V2.pin_7, Sensor_DHT22.DAT
  VIN: Heltec_WiFi_LoRa_32_V2.pin_16, Heltec_WiFi_LoRa_32_V2.pin_17, Transmissor.Vin, Sensor_DHT22.VCC
  N3: Heltec_WiFi_LoRa_32_V2.pin_18, Heltec_WiFi_LoRa_32_V2.pin_19, Transmissor.-, Sensor_DHT22.GND
  N4: Heltec_WiFi_LoRa_32_V2.pin_21, Heltec_WiFi_LoRa_32_V2.pin_22

custom parts:
  Heltec WiFi LoRa 32 V2: Heltec WiFi LoRa 32 V2 WiFi LoRa 32 is a classic IoT dev-board designed & produced by Heltec Automation(TM). It’s a highly integrated product based on ESP32 + SX127x, it has Wi-Fi, BLE, LoRa functions, also Li-Po battery management system, 0.96″ OLED are also included. It’s the best choice for smart cities, smart farms, smart home, and IoT makers.
  KY-005 Infrared Transmitter Module: Arduino IR Transmitter Module Keyes KY-005, emits infrared light at 38KHz.
  DHT22 module: DHT22 module. Pins GND VCC Data.

// code stored in the sketch: Untitled.ino
//Incluindo o arquivo da biblioteca que define a porta que será utilizada pelo transmissor infravermelho
#include "PinDefinitionsAndMore.h"

//Incluindo as bliotecas utilizadas
#include "WiFi.h"
#include "PubSubClient.h"
#include "ESPmDNS.h"
#include "DHTesp.h"
#include "heltec.h"
#include "IRremote.hpp"

//Definindo a Rede que o equipamento vai ser conectada
#define NET_SSID "LABProv"
#define NET_PASSWORD "laboprov1"

//Definindo os parâmetros do protocolo MQTT como ID, Broker, Porta e os Tópicos
#define MQTT_ID "ifresources-tcc-lora32"
#define MQTT_BROKER "broker.emqx.io"
#define MQTT_PORT 1883
#define MQTT_MILLIS_TOPIC "tcc_ifresources_millis"
#define MQTT_SECONDS_TOPIC "tcc_ifresources_seconds"
#define MQTT_DHT_TEMP_TOPIC "tcc_ifresources_temp"
#define MQTT_DHT_HUMD_TOPIC "tcc_ifresources_humd"
#define MQTT_NIVEL_TOPIC "tcc_ifresources_nivel"
#define MQTT_SENDRAW_TOPIC "tcc_ifresources_sendraw_manage"

//Definindo objeto para a conexão Wi-Fi e criação do cliente MQTT
WiFiClient espClient; 
PubSubClient MQTT(espClient);

//Definindo as Strings usadas para o envio das informações
char millis_str[10] = "";
char seconds_str[10] = "";
char temp_str[10] = "";
char humd_str[10] = "";
char nivel_str[10] = "";

//Definindo a banda de frequência de comunicação sem fio e definindo objeto para o DHT22 
#define BAND    915E6
DHTesp dht;

//Variavéis do Nivel d'água
using namespace std;
bool isPressed = "";
int nivel = 0;
int buttonState = 0;

//Variavéis do Sensor DHT22
float currentTemp;
float currentHumidity;

// Variável global para armazenar o tempo inicial
unsigned long tempoInicial;

//Definindo as funções
void getTemp();
void getHumidity();
void getNivel();
void sendPacket();

//Função que conecta o Lora 32 em algum Wi-Fi
void setupWifi(){
  if(WiFi.status() == WL_CONNECTED){
    return;
  } else {

    Serial.println();
    Serial.print("Connecting to ");
    Serial.println(NET_SSID);
  
    WiFi.begin(NET_SSID, NET_PASSWORD);

    while (WiFi.status() != WL_CONNECTED){
        delay(500);
        Serial.print(".");
    }

    Serial.println("");
    Serial.println("WiFi connected");
    Serial.println("IP Address:");
    Serial.println(WiFi.localIP());
    }
}

//Função que conecta o Lora 32 no Broker MQTT
void setupMQTT(){

    MQTT.setServer(MQTT_BROKER, MQTT_PORT);
    MQTT.setCallback(mqtt_ifresources_callback); 

    while (!MQTT.connected()){
        Serial.print("- MQTT Setup: Tentando se conectar ao Broker MQTT: ");
        Serial.println(MQTT_BROKER);

        if(MQTT.connect(MQTT_ID)){
            Serial.println("- MQTT Setup: Conectado com sucesso");
            Serial.println(" ");
             MQTT.subscribe(MQTT_SENDRAW_TOPIC);
        } else {
            Serial.println("- MQTT Setup: Falha ao se conectar, tentando novamente em 2s");
            delay(2000);
        }
    }
}

//Função da Temperatura
void getTemp()
{

  float temperature = dht.getTemperature();

  if (temperature != currentTemp) {
    currentTemp = temperature;

    digitalWrite(LED, HIGH);
    delay(500);
    digitalWrite(LED, LOW);
    delay(500);
  }
  delay(1000);
}

//Função da Umidade
void getHumidity()
{

  float humidity = dht.getHumidity();

  if (humidity != currentHumidity) {
    currentHumidity = humidity;
    
    digitalWrite(LED, HIGH);
    delay(500);
    digitalWrite(LED, LOW);
    delay(500);                
  }
  delay(1000);
}

//Função do Nível d'água
void getNivel()
{

    if (digitalRead(36) == 1)
    {
        nivel = 4;
    }
    
    else if (digitalRead(37) == 1)
    {
        nivel = 3;
    }

    else if (digitalRead(38) == 1)
    {
        nivel = 2;
    }

    else if (digitalRead(39) == 1)
    {
        nivel = 1;
    }
    else
    {
        nivel = 0;
    }

}

//Função setup aonde é definido a configuração da primeira tela e a pinagem de alguns componentes
void setup(void)
{
    /*O baudrate no monitor serial é (115200)*/
    tempoInicial = millis();
    pinMode(LED, OUTPUT);

    Heltec.begin(true, true, true , true , BAND);
    /*(
      true = Habilita o Display, 
      true = Heltec.Heltec.Heltec.LoRa Disable, 
      true = Habilita debug Serial, 
      true = Habilita o PABOOST, 
      BAND = Frequência BAND.
    )*/

    Heltec.display->init();
    Heltec.display->setContrast(255);
    Heltec.display->clear();
    Heltec.display->setFont(ArialMT_Plain_24);
    Heltec.display->drawString(0, 0, "IFresources");
    Heltec.display->setFont(ArialMT_Plain_16);
    Heltec.display->drawString(0, 25, "@ifrjniteroi");
    Heltec.display->setFont(ArialMT_Plain_10);
    Heltec.display->drawString(0, 45, "Conectando ao Wi-Fi...");
    Heltec.display->display();
    delay(1000);

    dht.setup(25, DHTesp::DHT22); 
  
    currentTemp = dht.getTemperature();
    currentHumidity = dht.getHumidity();

    pinMode(36, INPUT);
    pinMode(37, INPUT);
    pinMode(38, INPUT);
    pinMode(39, INPUT);

    setupWifi();
    setupMQTT();
}

//Função loop aonde é definido a configuração da segunda tela que mostra a temperatura e aonde é enviado as informações para o broker
void loop(void)
{
  getTemp();
  getHumidity();
  getNivel();

  unsigned long tempoAtual = millis();
  unsigned long segundos = (tempoAtual - tempoInicial) / 1000;

  Heltec.display->clear();
  Heltec.display->setTextAlignment(TEXT_ALIGN_LEFT);
  Heltec.display->setFont(ArialMT_Plain_16);
  Heltec.display->drawString(30, 5, "Temperatura");
  Heltec.display->drawString(33, 30, (String)currentTemp);
  Heltec.display->drawString(78, 30, "°C");
  Heltec.display->display();

  Serial.println("Tempo em Milissegundos: " + (String)millis());
  Serial.println("Tempo em Segundos: " + (String)segundos);  
  Serial.println("Temperatura: " + (String)currentTemp + "°C");
  Serial.println("Umidade: " + (String)currentHumidity + "%");
  Serial.println("Nivel da Água: " + (String)nivel);
  Serial.println("---");

  sprintf(millis_str, "%d", millis());
  MQTT.publish(MQTT_MILLIS_TOPIC, millis_str);

  sprintf(seconds_str, "%s", (String)segundos);
  MQTT.publish(MQTT_SECONDS_TOPIC, seconds_str);

  sprintf(temp_str, "%s", (String)currentTemp );
  MQTT.publish(MQTT_DHT_TEMP_TOPIC, temp_str);

  sprintf(humd_str, "%s", (String)currentHumidity );
  MQTT.publish(MQTT_DHT_HUMD_TOPIC, humd_str);

  sprintf(nivel_str, "%s", (String)nivel);
  MQTT.publish(MQTT_NIVEL_TOPIC, nivel_str);

  setupWifi();
  setupMQTT();
  MQTT.loop();
  delay(1000);
}

//Função Callback aonde é configurado os comandos do ar-condicionado de ligar, desligar, aumentar e diminuir a temperatura.
void mqtt_ifresources_callback(char* topic, byte* payload, unsigned int length)
{
  String msg;
  Serial.print("- MQTT Callback Topic: ");
  Serial.println(topic);

  for (int i = 0; i < length; i++)
  {
    char c = (char)payload[i];
    msg += c;
  }

  if (msg.equals("P1"))
    {
      #if !(defined(__AVR_ATtiny25__) || defined(__AVR_ATtiny45__) || defined(__AVR_ATtiny85__))
  
      const uint16_t rawData[] = {3064, 1624, 452, 1128, 452, 1124, 456, 360, 456, 360, 456, 360, 456, 1124, 456, 360, 452, 364, 452, 1128, 456, 1124, 456, 360, 456, 1124, 456, 360, 452, 364, 452, 1124, 456, 1124, 456, 360, 456, 1124, 456, 1124, 456, 360, 456, 360, 456, 1124, 452, 364, 456, 360, 456, 360, 452, 1128, 456, 360, 456, 360, 452, 360, 460, 360, 452, 364, 452, 360, 456, 360, 452, 364, 456, 360, 456, 360, 456, 360, 456, 360, 456, 360, 456, 360, 456, 360, 456, 360, 456, 360, 456, 360, 452, 364, 452, 360, 456, 1124, 456, 360, 456, 360, 456, 360, 456, 360, 456, 360, 456, 360, 456, 360, 456, 360, 456, 360, 456, 360, 452, 364, 452, 364, 452, 364, 452, 364, 452, 364, 452, 364, 452, 364, 452, 360, 456, 364, 452, 360, 456, 364, 452, 360, 456, 360, 452, 364, 452, 364, 452, 364, 456, 360, 452, 364, 452, 364, 456, 360, 452, 364, 456, 360, 452, 364, 452, 360, 452, 368, 452, 364, 452, 360, 456, 360, 452, 364, 452, 364, 452, 364, 456, 360, 456, 360, 452, 364, 456, 360, 456, 360, 456, 360, 452, 364, 452, 364, 456, 360, 456, 356, 456, 336, 480, 360, 456, 360, 456, 360, 456, 360, 456, 360, 456, 1124, 456, 360, 456, 1124, 456, 360, 452, 364, 452, 1124, 456, 1128, 452, 360, 456, 4456, 3060, 1628, 452, 1124, 456, 1124, 456, 360, 456, 360, 456, 360, 456, 1124, 456, 360, 456, 360, 452, 1128, 456, 1124, 456, 360, 452, 1128, 452, 360, 456, 360, 456, 1124, 456, 1124, 456, 360, 452, 1128, 456, 1124, 452, 364, 452, 364, 452, 1124, 456, 360, 456, 360, 456, 1124, 456, 360, 456, 360, 456, 360, 456, 360, 456, 360, 456, 360, 452, 364, 452, 364, 452, 364, 452, 364, 456, 360, 452, 364, 452, 364, 452, 364, 452, 364, 452, 364, 452, 360, 456, 1124, 456, 360, 456, 360, 452, 1128, 456, 360, 456, 360, 456, 1124, 452, 1128, 452, 364, 452, 364, 452, 364, 452, 364, 452, 364, 452, 360, 456, 1124, 456, 1124, 456, 360, 456, 1124, 452, 364, 456, 360, 456, 360, 456, 360, 452, 1128, 456, 1124, 452, 360, 456, 360, 456, 360, 456, 360, 456, 360, 452, 364, 456, 360, 456, 360, 456, 360, 456, 360, 456, 360, 456, 360, 452, 364, 456, 360, 452, 364, 452, 364, 452, 364, 452, 364, 452, 364, 452, 364, 452, 360, 456, 360, 452, 364, 456, 360, 456, 360, 456, 360, 456, 360, 456, 360, 456, 360, 456, 360, 452, 364, 456, 360, 452, 364, 452, 1128, 452, 360, 456, 360, 456, 360, 456, 1124, 456, 360, 456, 1124, 456, 360, 456, 360, 456, 1124, 456, 360, 456, 1120, 460, 1124, 452};
      IrSender.sendRaw(rawData, sizeof(rawData) / sizeof(rawData[0]), NEC_KHZ);
  
      Serial.println(F("Send NEC 16 bit address=0xFB04 and command 0x08 with exact timing (16 bit array format)"));
      Serial.flush();
      delay(1000);
      
        
      Serial.println("- MQTT Sub Conn: (P1) Ligar Ar-condicionado Received");
      Serial.println("---");

      #endif  
    }

   else if (msg.equals("P0"))
    {
      #if !(defined(__AVR_ATtiny25__) || defined(__AVR_ATtiny45__) || defined(__AVR_ATtiny85__))
  
      const uint16_t rawData[] = {3064, 1620, 456, 1124, 456, 1124, 456, 360, 456, 360, 456, 360, 456, 1124, 456, 360, 452, 364, 452, 1124, 460, 1124, 452, 360, 456, 1124, 456, 360, 456, 364, 452, 1124, 456, 1124, 456, 360, 452, 1128, 456, 1124, 452, 364, 452, 364, 456, 1124, 452, 360, 460, 356, 460, 356, 456, 1124, 456, 360, 456, 360, 456, 360, 456, 360, 456, 360, 456, 360, 452, 364, 456, 360, 456, 360, 456, 360, 456, 360, 456, 360, 456, 360, 456, 360, 456, 360, 452, 364, 452, 360, 460, 360, 456, 356, 456, 360, 456, 1124, 456, 360, 456, 360, 456, 360, 456, 360, 452, 364, 456, 360, 452, 364, 456, 360, 456, 360, 456, 360, 456, 356, 456, 364, 452, 360, 456, 360, 456, 360, 456, 360, 456, 360, 456, 360, 456, 360, 456, 360, 456, 360, 456, 360, 456, 360, 452, 364, 456, 360, 456, 360, 452, 360, 456, 364, 456, 356, 456, 360, 456, 360, 456, 360, 456, 360, 456, 360, 456, 360, 456, 360, 456, 360, 452, 364, 452, 364, 456, 360, 452, 364, 452, 364, 452, 360, 456, 360, 456, 364, 452, 360, 456, 360, 456, 360, 456, 360, 456, 360, 452, 364, 456, 360, 456, 360, 452, 364, 452, 364, 456, 356, 456, 364, 456, 1120, 456, 360, 456, 1124, 456, 360, 456, 360, 456, 1124, 456, 1124, 456, 360, 456, 3972, 3088, 1596, 484, 1096, 480, 1100, 480, 336, 480, 336, 452, 364, 480, 1100, 480, 336, 480, 336, 480, 1096, 484, 1096, 484, 332, 480, 1100, 480, 336, 480, 336, 480, 1100, 480, 1100, 480, 336, 480, 1096, 480, 1100, 480, 336, 480, 336, 484, 1096, 480, 336, 480, 336, 480, 1100, 480, 336, 480, 336, 480, 332, 484, 332, 484, 332, 480, 336, 480, 336, 480, 336, 480, 336, 480, 336, 480, 336, 480, 336, 484, 332, 480, 336, 480, 336, 480, 336, 480, 336, 480, 336, 480, 336, 480, 336, 476, 1100, 480, 336, 484, 332, 480, 1100, 452, 1128, 480, 336, 480, 336, 476, 340, 480, 336, 480, 332, 484, 332, 484, 1096, 484, 1096, 480, 336, 480, 1100, 480, 336, 480, 336, 480, 336, 452, 364, 480, 1100, 476, 1104, 480, 336, 480, 336, 476, 340, 476, 336, 480, 336, 484, 332, 480, 336, 456, 360, 480, 336, 480, 336, 480, 336, 480, 336, 480, 336, 480, 336, 480, 336, 480, 336, 480, 336, 480, 336, 480, 336, 480, 336, 452, 364, 480, 336, 476, 340, 480, 332, 484, 336, 476, 336, 480, 336, 480, 336, 480, 336, 480, 336, 480, 336, 452, 364, 480, 336, 476, 1104, 452, 364, 452, 364, 452, 364, 452, 1124, 456, 360, 452, 1128, 452, 1128, 452, 1124, 456, 360, 456, 364, 452, 1124, 452, 1128, 452};
      IrSender.sendRaw(rawData, sizeof(rawData) / sizeof(rawData[0]), NEC_KHZ); // Note the approach used to automatically calculate the size of the array.
  
      Serial.println(F("Send NEC 16 bit address=0xFB04 and command 0x08 with exact timing (16 bit array format)"));
      Serial.flush();
      delay(1000);
        
      Serial.println("- MQTT Sub Conn: (P0) Desligar Ar-condicionado Received");
      Serial.println("---");


      #endif
    }

    else if (msg.equals("A1"))
    {
      #if !(defined(__AVR_ATtiny25__) || defined(__AVR_ATtiny45__) || defined(__AVR_ATtiny85__))
  
      const uint16_t rawData[] = {3112, 1572, 456, 1124, 508, 1072, 504, 312, 456, 360, 504, 312, 504, 1076, 504, 312, 452, 364, 452, 1128, 504, 1072, 508, 312, 452, 1124, 508, 308, 456, 360, 508, 1072, 508, 1072, 456, 360, 504, 1076, 456, 1124, 504, 312, 452, 364, 452, 1128, 452, 364, 504, 312, 504, 312, 452, 1124, 456, 360, 456, 364, 452, 364, 452, 360, 456, 360, 508, 308, 508, 308, 456, 360, 508, 308, 456, 360, 452, 364, 456, 360, 508, 308, 452, 364, 456, 360, 504, 312, 504, 312, 504, 312, 452, 364, 452, 364, 452, 1124, 508, 312, 504, 312, 452, 364, 504, 312, 452, 360, 508, 308, 508, 308, 508, 308, 508, 308, 456, 360, 456, 360, 508, 308, 456, 360, 456, 360, 456, 364, 452, 360, 504, 312, 452, 364, 452, 364, 504, 312, 504, 312, 508, 308, 452, 364, 504, 312, 504, 312, 452, 364, 452, 364, 504, 312, 452, 360, 508, 308, 508, 308, 456, 360, 508, 308, 508, 308, 508, 308, 456, 360, 456, 360, 504, 312, 508, 308, 508, 308, 456, 360, 452, 364, 504, 312, 452, 364, 504, 312, 456, 360, 452, 364, 452, 364, 504, 312, 504, 312, 504, 312, 452, 360, 456, 364, 504, 308, 456, 360, 456, 360, 508, 308, 456, 1124, 456, 360, 504, 1076, 456, 360, 456, 360, 456, 1124, 452, 1128, 504, 312, 504, 3756, 3060, 1624, 460, 1120, 456, 1124, 508, 308, 456, 336, 480, 360, 456, 1124, 456, 360, 504, 312, 456, 1124, 456, 1124, 452, 364, 452, 1128, 504, 312, 452, 364, 452, 1128, 452, 1124, 456, 364, 452, 1124, 456, 1124, 456, 360, 456, 360, 456, 1124, 456, 360, 504, 312, 452, 1128, 504, 312, 504, 312, 452, 364, 452, 364, 452, 364, 504, 312, 452, 364, 452, 364, 452, 360, 456, 364, 452, 360, 508, 308, 456, 360, 456, 360, 456, 360, 456, 360, 456, 360, 452, 1128, 452, 364, 456, 360, 456, 1124, 456, 360, 452, 364, 452, 1128, 452, 1128, 452, 364, 452, 364, 452, 364, 460, 352, 456, 360, 456, 360, 456, 1124, 508, 1072, 456, 360, 452, 1128, 456, 360, 452, 364, 456, 360, 452, 364, 452, 1128, 452, 1128, 452, 360, 456, 364, 452, 360, 456, 360, 508, 308, 456, 360, 456, 360, 456, 360, 456, 360, 456, 360, 456, 360, 456, 360, 456, 360, 456, 360, 456, 360, 456, 360, 456, 360, 456, 360, 456, 360, 452, 340, 476, 364, 504, 312, 452, 364, 452, 364, 456, 360, 452, 364, 452, 364, 452, 360, 456, 360, 456, 364, 452, 360, 456, 360, 456, 360, 456, 1124, 456, 360, 456, 1124, 508, 308, 456, 1124, 452, 364, 456, 1124, 452, 364, 452, 364, 452, 1124, 456, 1124, 456, 1124, 456, 1124, 456};
      IrSender.sendRaw(rawData, sizeof(rawData) / sizeof(rawData[0]), NEC_KHZ); // Note the approach used to automatically calculate the size of the array.
  
      Serial.println(F("Send NEC 16 bit address=0xFB04 and command 0x08 with exact timing (16 bit array format)"));
      Serial.flush();
      delay(1000);
      
        
      Serial.println("- MQTT Sub Conn: (A1) Aumentar Temperatura Received");
      Serial.println("---");


      #endif  
    } 
    
    else if (msg.equals("D1"))
    {
      #if !(defined(__AVR_ATtiny25__) || defined(__AVR_ATtiny45__) || defined(__AVR_ATtiny85__))
  
      const uint16_t rawData[] = {3060, 1624, 456, 1124, 452, 1128, 452, 364, 452, 364, 452, 364, 452, 1128, 480, 332, 484, 336, 452, 1124, 456, 1124, 456, 360, 456, 1124, 456, 360, 452, 364, 456, 1124, 452, 1128, 452, 364, 452, 1128, 452, 1124, 456, 360, 456, 364, 452, 1124, 456, 360, 456, 360, 480, 336, 456, 1124, 480, 336, 452, 364, 452, 364, 452, 364, 452, 364, 452, 364, 452, 364, 452, 364, 452, 364, 452, 360, 456, 364, 452, 360, 484, 332, 456, 360, 456, 360, 456, 360, 456, 360, 456, 360, 456, 360, 456, 360, 456, 1124, 452, 364, 452, 364, 480, 336, 452, 364, 452, 364, 452, 360, 456, 364, 452, 360, 456, 364, 452, 360, 456, 364, 452, 360, 456, 360, 456, 360, 456, 360, 456, 360, 452, 364, 480, 336, 452, 364, 452, 364, 452, 364, 452, 364, 452, 364, 452, 364, 452, 364, 452, 360, 456, 360, 484, 332, 456, 360, 456, 360, 456, 360, 456, 360, 456, 360, 452, 364, 452, 364, 452, 364, 452, 364, 452, 364, 452, 364, 452, 364, 452, 360, 456, 360, 456, 360, 456, 360, 456, 360, 456, 360, 456, 360, 456, 360, 456, 360, 456, 360, 456, 360, 456, 360, 456, 360, 456, 360, 456, 360, 456, 360, 452, 364, 452, 1128, 452, 364, 452, 1128, 452, 360, 456, 360, 484, 1096, 456, 1124, 456, 360, 456, 4628, 3112, 1572, 456, 1124, 452, 1128, 456, 360, 452, 364, 504, 312, 456, 1124, 504, 312, 452, 364, 452, 1128, 452, 1128, 452, 360, 456, 1128, 500, 312, 456, 364, 452, 1124, 456, 1124, 452, 364, 452, 1128, 504, 1076, 504, 312, 452, 364, 456, 1124, 452, 364, 452, 364, 452, 1124, 456, 360, 508, 308, 456, 360, 504, 312, 504, 312, 508, 308, 504, 312, 452, 364, 504, 312, 456, 360, 504, 312, 456, 360, 504, 312, 504, 312, 452, 364, 452, 364, 452, 364, 452, 1128, 504, 308, 508, 308, 456, 1124, 456, 360, 504, 312, 456, 1124, 504, 1076, 452, 364, 452, 364, 452, 364, 456, 360, 452, 368, 448, 364, 452, 1124, 508, 1076, 452, 360, 508, 1072, 456, 360, 504, 312, 456, 360, 508, 308, 456, 1124, 456, 1124, 452, 364, 452, 364, 504, 312, 452, 364, 452, 364, 452, 364, 452, 364, 452, 364, 452, 360, 456, 364, 504, 308, 508, 312, 452, 360, 504, 312, 456, 360, 456, 360, 456, 360, 456, 360, 456, 360, 456, 360, 456, 360, 452, 364, 456, 360, 452, 364, 452, 364, 504, 312, 504, 312, 452, 364, 452, 364, 452, 360, 456, 364, 452, 364, 452, 360, 456, 1124, 508, 308, 456, 360, 456, 360, 504, 1076, 452, 364, 504, 1076, 456, 360, 452, 364, 452, 1128, 452, 360, 456, 1124, 456, 1124, 456};
      IrSender.sendRaw(rawData, sizeof(rawData) / sizeof(rawData[0]), NEC_KHZ);
  
      Serial.println(F("Send NEC 16 bit address=0xFB04 and command 0x08 with exact timing (16 bit array format)"));
      Serial.flush();
      delay(1000);
      
      
      Serial.println("- MQTT Sub Conn: (D1) Diminuir Temperatura Received");
      Serial.println("---");

      #endif
    }
}
